// Logisim project Hamming_Code_3bit.circ as structural Verilog: 1 circuit, main circuit main
module main (
);

  wire button_1_out, decoder_1_out1, decoder_1_out2, decoder_1_out3, decoder_1_out4, decoder_1_out5,
       decoder_1_out6, decoder_2_out3, decoder_2_out5, decoder_2_out6;
  wire [2:0] counter_1_q, D1_out, xor_7_out;
  wire [3:0] Tx, TxErr;
  wire [5:0] Rx;

  xor xor_1 (Tx[0], 1'b1, 1'b0);
  xor xor_2 (Tx[3], 1'b0, 1'b1);
  xor xor_3 (Rx[0], Rx[2], Rx[4]);
  xor xor_4 (Rx[3], Rx[4], Rx[5]);
  xor xor_5 (Tx[1], Tx[0], 1'b1);
  xor xor_6 (Rx[1], Rx[0], Rx[5]);
  Button button_1 (.out(button_1_out));
  xor xor_7 (xor_7_out[0], Rx[0], TxErr[0]);
  xor xor_8 (xor_7_out[1], Rx[1], TxErr[1]);
  xor xor_9 (xor_7_out[2], Rx[3], TxErr[3]);
  Decoder #(.select(3)) decoder_1 (
    .out1(decoder_1_out1), .out2(decoder_1_out2), .out3(decoder_1_out3), .out4(decoder_1_out4),
    .out5(decoder_1_out5), .out6(decoder_1_out6), .sel(counter_1_q));  // open: out0, out7, en
  Counter #(.width(3), .max('h7)) counter_1 (.Q(counter_1_q), .clk(button_1_out));  // open: load, D, count, carry, clr
  Decoder #(.select(3)) decoder_2 (
    .out3(decoder_2_out3), .out5(decoder_2_out5), .out6(decoder_2_out6), .sel(xor_7_out));  // open: out0, out1, out2, out4, out7, en
  xor D1 (D1_out[0], decoder_2_out3, Rx[2]);
  xor D2 (D1_out[1], decoder_2_out5, Rx[4]);
  xor D3 (D1_out[2], decoder_2_out6, Rx[5]);
  xor P1 (TxErr[0], decoder_1_out1, Tx[0]);
  xor P2 (TxErr[1], decoder_1_out2, Tx[1]);
  xor D1_2 (Rx[2], decoder_1_out3, 1'b1);
  xor P3 (TxErr[3], decoder_1_out4, Tx[3]);
  xor D2_2 (Rx[4], decoder_1_out5, 1'b0);
  xor D3_2 (Rx[5], decoder_1_out6, 1'b1);
  Hex_Digit_Display hex_digit_display_1 (.value({1'b0, D1_out}));  // open: dp

  // Other names for the same wires on the sheet: TxErr (some bits) = {Rx[5:4], Rx[2]}

  // Notes on the sheet:
  //   Hamming Code 3 bit parity
  //   P1
  //   P2
  //   P3
  //   P1
  //   P3
  //   P2
endmodule
