// Logisim project Hamming_Code_4bit.circ as structural Verilog: 1 circuit, main circuit main
module main (
  input  D1,
  input  D2,
  input  D3,
  input  D4,
  input  in_5,
  input  in_6
);

  wire button_1_out, demultiplexer_1_out1, demultiplexer_1_out2, demultiplexer_1_out3, demultiplexer_1_out4,
       demultiplexer_1_out5, demultiplexer_1_out6, demultiplexer_1_out7, demultiplexer_2_out1,
       demultiplexer_2_out2, demultiplexer_2_out3, demultiplexer_2_out4, demultiplexer_2_out5,
       demultiplexer_2_out6, demultiplexer_2_out7, xor_1_out, xor_2_out, xor_3_out, xor_4_out, xor_8_out,
       xor_9_out, xor_10_out, xor_12_out, xor_13_out;
  wire [2:0] counter_1_q, xor_11_out;
  wire [3:0] DwP;
  wire [6:0] DataOut, DataWithError;

  xor xor_1 (xor_1_out, D1, D2);
  xor xor_2 (xor_2_out, D1, D3);
  xor xor_3 (xor_3_out, D3, D4);
  xor xor_4 (xor_4_out, DataWithError[2], DataWithError[4]);
  xor xor_5 (DwP[0], xor_1_out, D4);
  xor xor_6 (DwP[1], xor_2_out, D4);
  xor xor_7 (DwP[3], xor_3_out, D2);
  xor xor_8 (xor_8_out, xor_4_out, DataWithError[6]);
  xor xor_9 (xor_9_out, DataWithError[2], DataWithError[5]);
  xor xor_10 (xor_10_out, DataWithError[4], DataWithError[5]);
  Button button_1 (.out(button_1_out));
  xor xor_11 (xor_11_out[0], xor_8_out, DataWithError[0]);
  xor xor_12 (xor_12_out, xor_9_out, DataWithError[6]);
  xor xor_13 (xor_13_out, xor_10_out, DataWithError[6]);
  Demultiplexer #(.select(3)) demultiplexer_1 (
    .out1(demultiplexer_1_out1), .out2(demultiplexer_1_out2), .out3(demultiplexer_1_out3),
    .out4(demultiplexer_1_out4), .out5(demultiplexer_1_out5), .out6(demultiplexer_1_out6),
    .out7(demultiplexer_1_out7), .in(in_5), .sel(counter_1_q));  // open: out0, en
  Counter #(.width(3), .max('h7)) counter_1 (.Q(counter_1_q), .clk(button_1_out));  // open: load, D, count, carry, clr
  xor xor_14 (xor_11_out[1], xor_12_out, DataWithError[1]);
  xor xor_15 (xor_11_out[2], xor_13_out, DataWithError[3]);
  Demultiplexer #(.select(3)) demultiplexer_2 (
    .out1(demultiplexer_2_out1), .out2(demultiplexer_2_out2), .out3(demultiplexer_2_out3),
    .out4(demultiplexer_2_out4), .out5(demultiplexer_2_out5), .out6(demultiplexer_2_out6),
    .out7(demultiplexer_2_out7), .in(in_6), .sel(xor_11_out));  // open: out0, en
  xor xor_16 (DataWithError[0], demultiplexer_1_out1, DwP[0]);
  xor xor_17 (DataWithError[1], demultiplexer_1_out2, DwP[1]);
  xor xor_18 (DataWithError[2], demultiplexer_1_out3, D1);
  xor xor_19 (DataWithError[3], demultiplexer_1_out4, DwP[3]);
  xor xor_20 (DataWithError[4], demultiplexer_1_out5, D2);
  xor xor_21 (DataWithError[5], demultiplexer_1_out6, D3);
  xor xor_22 (DataWithError[6], demultiplexer_1_out7, D4);
  xor xor_23 (DataOut[0], demultiplexer_2_out1, DataWithError[0]);
  xor xor_24 (DataOut[1], demultiplexer_2_out2, DataWithError[1]);
  xor xor_25 (DataOut[2], demultiplexer_2_out3, DataWithError[2]);
  xor xor_26 (DataOut[3], demultiplexer_2_out4, DataWithError[3]);
  xor xor_27 (DataOut[4], demultiplexer_2_out5, DataWithError[4]);
  xor xor_28 (DataOut[5], demultiplexer_2_out6, DataWithError[5]);
  xor xor_29 (DataOut[6], demultiplexer_2_out7, DataWithError[6]);
  Hex_Digit_Display hex_digit_display_1 (.value({DataOut[2], DataOut[4], DataOut[5], DataOut[6]}));  // open: dp

  // Other names for the same wires on the sheet: P1 = DwP[0]; P2 = DwP[1]; DwP (some bits) = {D4, D3, D2, D1};
  //   P3 = DwP[3]

  // Notes on the sheet:
  //   Hamming Code Parity Generator with Error Correction
endmodule
